# Fritzing sketch 전람회 회로도 1 (saved by Fritzing 0.9.3b)
breadboards: 1

parts:
  부품1 = Arduino Uno (Rev3)
  부품2 = Bluetooth HC-05 Macho
  RHT1 = Humidity and Temperature Sensor RHT03
  J2 = Basic Servo
  J3 = Basic Servo
  LCD1 = LCD screen  # not connected
  J1 = Basic Servo

nets:
  N1: 부품1.D8, 부품2.TXD
  N2: 부품1.D9_PWM, RHT1.Data-signal
  N3: 부품1.D3_PWM, J3.pulse
  N4: 부품1.D4, J2.pulse
  N5: 부품1.D5_PWM, J1.pulse
  N6: 부품1.D7, 부품2.RXD
  VCC: 부품1.5V, 부품2.VCC, RHT1.Vcc, J2.vcc, J3.vcc, J1.vcc
  GND: 부품1.GND, 부품2.GND, RHT1.GND_2, J2.gnd, J3.gnd, J1.gnd
